# Fritzing sketch printing_PCB (saved by Fritzing 0.9.3b)
circuit board: 4.29036cm x 2.24982cm
breadboards: 1

parts:
  Part1 = Adafruit TSL2561 [part_number="Adafruit #439"]
  J1 = female pin header, 5 pins [form="♀ (female)"]

nets:
  N1: Part1.VIN, J1.pin1
  N2: Part1.GND, J1.pin5
  N3: Part1.SDA, J1.pin2
  N4: Part1.SCL, J1.pin3

notes:
  Vin
  GND
  SDA
  SCL
  Harsimran Saini
  TSL2561

custom parts:
  Adafruit TSL2561: The TSL2561 luminosity sensor is an advanced digital light sensor, ideal for use in a wide range of light situations. Compared to low cost CdS cells, this sensor is more precise, allowing for exact lux calculations and can be configured for different gain/timing ranges to detect light ranges from up to 0.1 - 40,000+ Lux on the fly. The best part of this sensor is that it contains both infrared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
