# Fritzing sketch with_raspberrypi (saved by Fritzing 0.9.3b)
circuit board: 2.78878cm x 3.83964cm
breadboards: 1

parts:
  Raspberry_Pi_Zero1 = Raspberry Pi Zero
  Tsl2561 = Adafruit TSL2561 [part_number="Adafruit #439"]

nets:
  3V3: Raspberry_Pi_Zero1.3v3, Tsl2561.VIN
  N1: Raspberry_Pi_Zero1.GPIO2, Tsl2561.SDA
  N2: Raspberry_Pi_Zero1.GPIO3, Tsl2561.SCL
  GND: Raspberry_Pi_Zero1.GND, Tsl2561.GND

notes:
  n01246904
  Saini
  Harsimran

custom parts:
  Adafruit TSL2561: The TSL2561 luminosity sensor is an advanced digital light sensor, ideal for use in a wide range of light situations. Compared to low cost CdS cells, this sensor is more precise, allowing for exact lux calculations and can be configured for different gain/timing ranges to detect light ranges from up to 0.1 - 40,000+ Lux on the fly. The best part of this sensor is that it contains both infrared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
